# Fritzing sketch aula03_2-ex1 (saved by Fritzing 0.9.4)
breadboards: 2

parts:
  VCC1 = Battery block 9V
  Digital_Panel_Meter_Voltage_DMS-20PC_by_Murata1 = Digital Panel Meter, Voltage, DMS-20PC
  VCC2 = Battery block 9V
  Digital_Panel_Meter_Voltage_DMS-20PC_by_Murata2 = Digital Panel Meter, Voltage, DMS-20PC
  Digital_Panel_Meter_Voltage_DMS-20PC_by_Murata3 = Digital Panel Meter, Voltage, DMS-20PC
  VCC3 = Battery block 9V

nets:
  N1: VCC1.-, Digital_Panel_Meter_Voltage_DMS-20PC_by_Murata1.12:_(-)_INPUT_LO
  N2: VCC1.+, Digital_Panel_Meter_Voltage_DMS-20PC_by_Murata1.11:_(+)_INPUT_HI
  N3: VCC2.-, Digital_Panel_Meter_Voltage_DMS-20PC_by_Murata2.12:_(-)_INPUT_LO
  N4: VCC2.+, Digital_Panel_Meter_Voltage_DMS-20PC_by_Murata2.11:_(+)_INPUT_HI
  N5: Digital_Panel_Meter_Voltage_DMS-20PC_by_Murata3.11:_(+)_INPUT_HI, VCC3.-
  N6: Digital_Panel_Meter_Voltage_DMS-20PC_by_Murata3.12:_(-)_INPUT_LO, VCC3.+
