# Fritzing sketch aula03_2-ex3 (saved by Fritzing 0.9.4)
breadboards: 1

parts:
  R1 = Resistor [tolerance=±5% resistance=220 package=THT]
  LED1 = LED - 5mm [color="Red (633nm)" package="5 mm [THT]"]
  VCC1 = Battery block 9V

nets:
  N1: R1.Pin_0, VCC1.-
  N2: R1.Pin_1, LED1.cathode
  N3: LED1.anode, VCC1.+
