# Fritzing sketch aula03_2-ex4 (saved by Fritzing 0.9.4)
breadboards: 1

parts:
  Part2 = Arduino Uno (Rev3) - ICSP
  LED2 = LED - 5mm [color="Red (633nm)" package="5 mm [THT]"]
  R1 = Resistor [tolerance=±5% resistance=220 package=THT]

nets:
  N1: Part2.GND, LED2.cathode
  N2: Part2.D7, R1.Pin_1
  N3: LED2.anode, R1.Pin_0
