# Fritzing sketch aula03_2-ex5 (saved by Fritzing 0.9.4)
breadboards: 1

parts:
  Part3 = Arduino Uno (Rev3) - ICSP
  LED3 = LED - 5mm [color="Red (633nm)" package="5 mm [THT]"]
  R2 = Resistor [tolerance=±5% resistance=220 package=THT]
  R3 = Resistor [tolerance=±5% resistance=220 package=THT]
  LED4 = LED - 5mm [color="Red (633nm)" package="5 mm [THT]"]

nets:
  N1: Part3.D8, R3.Pin_1
  N2: Part3.GND, LED3.cathode, LED4.cathode
  N3: Part3.D7, R2.Pin_1
  N4: LED3.anode, R2.Pin_0
  N5: R3.Pin_0, LED4.anode
